// Logisim project  Parity_generator_and_checker_circuit.circ as structural Verilog: 1 circuit, main circuit main
module main (
  input  A,
  input  B,
  input  C,
  input  A_2,
  input  B_2,
  input  C_2,
  input  A_3,
  input  B_3,
  input  C_3,
  input  P,
  output Even_Parity,
  output Odd_Parity,
  output Checker
);

  wire dip_7486_1_p3, dip_7486_2_p3, dip_7486_2_p6, dip_7486_3_p1, dip_7486_3_p6;

  // DIP_7486 dip_7486_1: pin names not known; wires that end beside it: B, A, dip_7486_1_p3, dip_7486_1_p3, C, Even_Parity
  // DIP_7486 dip_7486_2: pin names not known; wires that end beside it: B_2, A_2, dip_7486_2_p3, dip_7486_2_p3, C_2, dip_7486_2_p6
  // DIP_7486 dip_7486_3: pin names not known; wires that end beside it: dip_7486_3_p1, B_3, P, A_3, Checker, dip_7486_3_p6, dip_7486_3_p6, C_3, dip_7486_3_p1
  // DIP_7404 dip_7404_1: pin names not known; wires that end beside it: dip_7486_2_p6, Odd_Parity, Checker, Odd_Parity
endmodule
