// Logisim project 3 to 14 into Excess-N(7) code[only NAND IC].circ as structural Verilog: 1 circuit, main circuit main
// P
module main (
  input  D,
  input  C,
  input  B,
  input  A,
  output P,
  output Q,
  output R,
  output S,
  output out_9
);

  wire dip_7400_1_p3, dip_7400_1_p8, dip_7400_2_p4, dip_7400_2_p6, dip_7400_2_p8, dip_7400_2_p12,
       dip_7400_3_p3, dip_7400_3_p5, dip_7400_4_p1, dip_7400_4_p6, dip_7400_4_p7, dip_7400_7_p3,
       dip_7410_1_p4;

  // DIP_7400 dip_7400_1: pin names not known; wires that end beside it: A, A, dip_7400_1_p3, B, D, B, D, dip_7400_1_p8, out_9
  // DIP_7410 dip_7410_1: pin names not known; wires that end beside it: dip_7400_1_p8, dip_7400_1_p3, out_9, dip_7410_1_p4
  // DIP_7400 dip_7400_2: pin names not known; wires that end beside it: C, D, D, dip_7400_2_p4, dip_7400_2_p4, dip_7400_2_p6, C, dip_7400_2_p8, dip_7400_2_p4, dip_7400_2_p6, dip_7400_2_p8, dip_7400_2_p12
  // DIP_7400 dip_7400_3: pin names not known; wires that end beside it: dip_7400_1_p3, out_9, dip_7400_3_p3, B, dip_7400_3_p5, dip_7400_3_p3, dip_7410_1_p4, dip_7400_3_p5, R
  // DIP_7400 dip_7400_4: pin names not known; wires that end beside it: dip_7400_4_p1, dip_7400_1_p3, dip_7400_4_p1, dip_7400_1_p8, out_9, dip_7400_4_p6, dip_7400_4_p7
  // DIP_7400 dip_7400_5: pin names not known; wires that end beside it: A, dip_7410_1_p4, Q
  // DIP_7400 dip_7400_6: pin names not known; wires that end beside it: dip_7400_2_p12, dip_7400_2_p12, S
  // DIP_7400 dip_7400_7: pin names not known; wires that end beside it: dip_7400_4_p7, A, dip_7400_7_p3, dip_7400_7_p3, dip_7400_7_p3, P
endmodule
