// Logisim project 4x1 MUX Full Adder.circ as structural Verilog: 1 circuit, main circuit main
module main (
  input  C,
  input  in_2,
  input  in_3,
  input  [1:0] A_B,
  output SUM,
  output COUT
);

  wire not_1_out;

  not not_1 (not_1_out, C);
  Multiplexer #(.select(2), .enable("false")) multiplexer_1 (
    .in0(C), .in1(not_1_out), .in2(not_1_out), .in3(C), .out(SUM), .sel(A_B));
  Multiplexer #(.select(2), .enable("false")) multiplexer_2 (
    .in0(in_2), .in1(C), .in2(C), .in3(in_3), .out(COUT), .sel(A_B));
endmodule
