// Logisim project BCD_to_excess-3 conversion_circuit.circ as structural Verilog: 1 circuit, main circuit main
module main (
  input  B0,
  input  B1,
  input  B2,
  input  B3,
  output E3,
  output E2,
  output E1,
  output E0
);

  wire dip_7432_1_p3, dip_7432_1_p5, dip_7486_1_p5;

  // DIP_7432 dip_7432_1: pin names not known; wires that end beside it: B1, B0, dip_7432_1_p3, B3, dip_7432_1_p5, E3
  // DIP_7408 dip_7408_1: pin names not known; wires that end beside it: B2, dip_7432_1_p3, dip_7432_1_p5
  // DIP_7486 dip_7486_1: pin names not known; wires that end beside it: B0, B2, B1, dip_7432_1_p3, dip_7486_1_p5, E2
  // DIP_7404 dip_7404_1: pin names not known; wires that end beside it: B0, dip_7486_1_p5, E0, E1
endmodule
