// Logisim project Basic_Gates_Using_NOR_Gate.circ as structural Verilog: 1 circuit, main circuit main
module main (
  input  A,
  input  A_2,
  input  B,
  input  A_3,
  input  B_2,
  output NOT,
  output OR,
  output AND
);

  wire dip_7402_2_p1, dip_7402_3_p1, dip_7402_3_p6;

  // DIP_7402 dip_7402_1: pin names not known; wires that end beside it: NOT, A, A
  // DIP_7402 dip_7402_2: pin names not known; wires that end beside it: dip_7402_2_p1, OR, A_2, dip_7402_2_p1, B, dip_7402_2_p1
  // DIP_7402 dip_7402_3: pin names not known; wires that end beside it: dip_7402_3_p1, AND, A_3, dip_7402_3_p1, A_3, dip_7402_3_p6, dip_7402_3_p6, B_2, B_2
endmodule
