// Logisim project Full_Adder_Implementation.circ as structural Verilog: 1 circuit, main circuit main
module main (
  input  A,
  input  B,
  input  Cin,
  output SUM,
  output Carry_out
);

  wire dip_7408_1_p3, dip_7408_1_p6, dip_7486_1_p3;

  // DIP_7486 dip_7486_1: pin names not known; wires that end beside it: B, A, dip_7486_1_p3, dip_7486_1_p3, Cin, SUM
  // DIP_7408 dip_7408_1: pin names not known; wires that end beside it: Cin, dip_7486_1_p3, dip_7408_1_p3, A, B, dip_7408_1_p6
  // DIP_7432 dip_7432_1: pin names not known; wires that end beside it: dip_7408_1_p6, dip_7408_1_p3, Carry_out, SUM, Carry_out
endmodule
