// Logisim project Full_Subtractor_Implementation.circ as structural Verilog: 1 circuit, main circuit main
module main (
  input  A,
  input  B,
  input  Bin,
  output out_4,
  output B0
);

  wire dip_7404_1_p2, dip_7404_1_p4, dip_7408_1_p3, dip_7408_1_p6, dip_7486_1_p3;

  // DIP_7486 dip_7486_1: pin names not known; wires that end beside it: B, A, dip_7486_1_p3, dip_7486_1_p3, Bin, out_4
  // DIP_7404 dip_7404_1: pin names not known; wires that end beside it: A, dip_7404_1_p2, dip_7486_1_p3, dip_7404_1_p4
  // DIP_7408 dip_7408_1: pin names not known; wires that end beside it: dip_7404_1_p2, B, dip_7408_1_p3, dip_7404_1_p4, Bin, dip_7408_1_p6, out_4
  // DIP_7432 dip_7432_1: pin names not known; wires that end beside it: dip_7408_1_p6, dip_7408_1_p3, B0, B0
endmodule
