// Logisim project basic_gate_implementation_using_NAND_gate_IC.circ as structural Verilog: 1 circuit, main circuit main
module main (
  input  in_1,
  input  in_2,
  input  in_3,
  input  in_4,
  input  in_5,
  output out_6,
  output out_7,
  output out_8
);

  wire dip_7400_1_p5, dip_7400_1_p6, dip_7400_3_p3;

  // DIP_7400 dip_7400_1: pin names not known; wires that end beside it: in_5, in_4, in_5, in_4, dip_7400_1_p5, dip_7400_1_p6, dip_7400_1_p5, dip_7400_1_p6, out_8
  // DIP_7400 dip_7400_2: pin names not known; wires that end beside it: in_1, in_1, out_6
  // DIP_7400 dip_7400_3: pin names not known; wires that end beside it: in_2, in_3, dip_7400_3_p3, dip_7400_3_p3, dip_7400_3_p3, out_7
endmodule
